// Logisim project DFlipFlop.circ as structural Verilog: 17 circuits, main circuit D8bitRegister
module D8bitRegister (
  input  Cl,
  input  E,
  input  [7:0] Num,
  output [7:0] Q,
  output [7:0] QN
);

  CDflipFlop cdflipflop_1 (.C(Cl), .D(Num[0]), .E(E), .Q(Q[0]), .QN(QN[0]));
  CDflipFlop cdflipflop_2 (.C(Cl), .D(Num[1]), .E(E), .Q(Q[1]), .QN(QN[1]));
  CDflipFlop cdflipflop_3 (.C(Cl), .D(Num[2]), .E(E), .Q(Q[2]), .QN(QN[2]));
  CDflipFlop cdflipflop_4 (.C(Cl), .D(Num[3]), .E(E), .Q(Q[3]), .QN(QN[3]));
  CDflipFlop cdflipflop_5 (.C(Cl), .D(Num[4]), .E(E), .Q(Q[4]), .QN(QN[4]));
  CDflipFlop cdflipflop_6 (.C(Cl), .D(Num[5]), .E(E), .Q(Q[5]), .QN(QN[5]));
  CDflipFlop cdflipflop_7 (.C(Cl), .D(Num[6]), .E(E), .Q(Q[6]), .QN(QN[6]));
  CDflipFlop cdflipflop_8 (.C(Cl), .D(Num[7]), .E(E), .Q(Q[7]), .QN(QN[7]));
endmodule

module CDflipFlop (
  input  C,
  input  D,
  input  E,
  output Q,
  output QN
);

  wire cmux2x1_1_o, nand_1_out, nand_2_out, nand_3_out, nand_4_out, nand_5_out, nand_6_out, not_1_out,
       not_2_out, not_3_out;

  not not_1 (not_1_out, C);
  not not_2 (not_2_out, cmux2x1_1_o);
  nand nand_1 (nand_1_out, not_2_out, C);
  not not_3 (not_3_out, nand_5_out);
  nand nand_2 (nand_2_out, cmux2x1_1_o, C);
  nand nand_3 (nand_3_out, not_3_out, not_1_out);
  nand nand_4 (nand_4_out, nand_5_out, not_1_out);
  nand nand_5 (nand_5_out, nand_2_out, nand_6_out);
  nand nand_6 (nand_6_out, nand_5_out, nand_1_out);
  nand nand_7 (Q, nand_4_out, QN);
  Cmux2x1 cmux2x1_1 (.N(D), .P(Q), .S(E), .O(cmux2x1_1_o));
  nand nand_8 (QN, Q, nand_3_out);
endmodule

module Cmux2x1 (
  input  N,
  input  P,
  input  S,
  output O
);

  wire and_1_out, and_2_out, not_1_out;

  not not_1 (not_1_out, S);
  and and_1 (and_1_out, N, S);
  and and_2 (and_2_out, P, not_1_out);
  or or_1 (O, and_1_out, and_2_out);
endmodule

module GG (
  input  [2:0] in_1,
  input  in_2,
  input  [2:0] in_3,
  input  [2:0] in_4,
  input  in_5,
  input  in_6,
  input  [2:0] in_7,
  input  imm,
  input  [31:0] in_9,
  output [31:0] out_10,
  output [31:0] out_11,
  output [31:0] out_12
);

  wire [31:0] c32bit2x1mux_1_o;

  C32Bit2x1Mux c32bit2x1mux_1 (.N(in_9), .P(out_12), .S(imm), .O(c32bit2x1mux_1_o));
  C32BitALU c32bitalu_1 (
    .opcode(in_1), .B(c32bit2x1mux_1_o), .A(out_11), .ModeAsr(in_2), .O(out_10));  // open: SF, ZF, CF, OVF
  C32BitRegisterFile c32bitregisterfile_1 (
    .C(in_5), .R(out_10), .SA(in_3), .EW(in_6), .SR(in_7), .SB(in_4), .A(out_11), .B(out_12));
endmodule

module D16BitRegister (
  input  C,
  input  E,
  input  [15:0] Num,
  output [15:0] Q,
  output [15:0] QN
);

  D8bitRegister d8bitregister_1 (.Cl(C), .E(E), .Num(Num[15:8]), .Q(Q[15:8]), .QN(QN[15:8]));
  D8bitRegister d8bitregister_2 (.Cl(C), .E(E), .Num(Num[7:0]), .Q(Q[7:0]), .QN(QN[7:0]));
endmodule

module D32bitRegister (
  input  E,
  input  C,
  input  [31:0] Num,
  output [31:0] QN,
  output [31:0] Q
);

  D16BitRegister d16bitregister_1 (.C(C), .E(E), .Num(Num[31:16]), .Q(Q[31:16]), .QN(QN[31:16]));
  D16BitRegister d16bitregister_2 (.C(C), .E(E), .Num(Num[15:0]), .Q(Q[15:0]), .QN(QN[15:0]));
endmodule

module C32Bit2x1Mux (
  input  [31:0] N,
  input  [31:0] P,
  input  S,
  output [31:0] O
);

  Cmux2x1 cmux2x1_1 (.N(N[0]), .P(P[0]), .S(S), .O(O[0]));
  Cmux2x1 cmux2x1_2 (.N(N[1]), .P(P[1]), .S(S), .O(O[1]));
  Cmux2x1 cmux2x1_3 (.N(N[2]), .P(P[2]), .S(S), .O(O[2]));
  Cmux2x1 cmux2x1_4 (.N(N[3]), .P(P[3]), .S(S), .O(O[3]));
  Cmux2x1 cmux2x1_5 (.N(N[4]), .P(P[4]), .S(S), .O(O[4]));
  Cmux2x1 cmux2x1_6 (.N(N[5]), .P(P[5]), .S(S), .O(O[5]));
  Cmux2x1 cmux2x1_7 (.N(N[6]), .P(P[6]), .S(S), .O(O[6]));
  Cmux2x1 cmux2x1_8 (.N(N[7]), .P(P[7]), .S(S), .O(O[7]));
  Cmux2x1 cmux2x1_9 (.N(N[8]), .P(P[8]), .S(S), .O(O[8]));
  Cmux2x1 cmux2x1_10 (.N(N[9]), .P(P[9]), .S(S), .O(O[9]));
  Cmux2x1 cmux2x1_11 (.N(N[10]), .P(P[10]), .S(S), .O(O[10]));
  Cmux2x1 cmux2x1_12 (.N(N[11]), .P(P[11]), .S(S), .O(O[11]));
  Cmux2x1 cmux2x1_13 (.N(N[12]), .P(P[12]), .S(S), .O(O[12]));
  Cmux2x1 cmux2x1_14 (.N(N[13]), .P(P[13]), .S(S), .O(O[13]));
  Cmux2x1 cmux2x1_15 (.N(N[14]), .P(P[14]), .S(S), .O(O[14]));
  Cmux2x1 cmux2x1_16 (.N(N[15]), .P(P[15]), .S(S), .O(O[15]));
  Cmux2x1 cmux2x1_17 (.N(N[16]), .P(P[16]), .S(S), .O(O[16]));
  Cmux2x1 cmux2x1_18 (.N(N[17]), .P(P[17]), .S(S), .O(O[17]));
  Cmux2x1 cmux2x1_19 (.N(N[18]), .P(P[18]), .S(S), .O(O[18]));
  Cmux2x1 cmux2x1_20 (.N(N[19]), .P(P[19]), .S(S), .O(O[19]));
  Cmux2x1 cmux2x1_21 (.N(N[20]), .P(P[20]), .S(S), .O(O[20]));
  Cmux2x1 cmux2x1_22 (.N(N[21]), .P(P[21]), .S(S), .O(O[21]));
  Cmux2x1 cmux2x1_23 (.N(N[22]), .P(P[22]), .S(S), .O(O[22]));
  Cmux2x1 cmux2x1_24 (.N(N[23]), .P(P[23]), .S(S), .O(O[23]));
  Cmux2x1 cmux2x1_25 (.N(N[24]), .P(P[24]), .S(S), .O(O[24]));
  Cmux2x1 cmux2x1_26 (.N(N[25]), .P(P[25]), .S(S), .O(O[25]));
  Cmux2x1 cmux2x1_27 (.N(N[26]), .P(P[26]), .S(S), .O(O[26]));
  Cmux2x1 cmux2x1_28 (.N(N[27]), .P(P[27]), .S(S), .O(O[27]));
  Cmux2x1 cmux2x1_29 (.N(N[28]), .P(P[28]), .S(S), .O(O[28]));
  Cmux2x1 cmux2x1_30 (.N(N[29]), .P(P[29]), .S(S), .O(O[29]));
  Cmux2x1 cmux2x1_31 (.N(N[30]), .P(P[30]), .S(S), .O(O[30]));
  Cmux2x1 cmux2x1_32 (.N(N[31]), .P(P[31]), .S(S), .O(O[31]));
endmodule

module C32BitLeftShifter (
  input  [4:0] S,
  input  [31:0] P,
  output [31:0] O
);

  wire [0:0] pull_resistor_1_node;
  wire [1:1] pull_resistor_2_node;
  wire [3:3] pull_resistor_3_node;
  wire [7:7] pull_resistor_4_node;
  wire [15:15] pull_resistor_5_node;
  wire [31:0] c32bit2x1mux_1_o, c32bit2x1mux_2_o, c32bit2x1mux_3_o, c32bit2x1mux_4_o;

  Pull_Resistor pull_resistor_1 (.node(pull_resistor_1_node[0]));
  C32Bit2x1Mux c32bit2x1mux_1 (.N({P[30:0], pull_resistor_1_node[0]}), .P(P), .S(S[0]), .O(c32bit2x1mux_1_o));
  Pull_Resistor pull_resistor_2 (.node(pull_resistor_2_node[1]));
  C32Bit2x1Mux c32bit2x1mux_2 (
    .N({c32bit2x1mux_1_o[29:0], {2{pull_resistor_2_node[1]}}}), .P(c32bit2x1mux_1_o), .S(S[1]),
    .O(c32bit2x1mux_2_o));
  Pull_Resistor pull_resistor_3 (.node(pull_resistor_3_node[3]));
  C32Bit2x1Mux c32bit2x1mux_3 (
    .N({c32bit2x1mux_2_o[27:0], {4{pull_resistor_3_node[3]}}}), .P(c32bit2x1mux_2_o), .S(S[2]),
    .O(c32bit2x1mux_3_o));
  Pull_Resistor pull_resistor_4 (.node(pull_resistor_4_node[7]));
  C32Bit2x1Mux c32bit2x1mux_4 (
    .N({c32bit2x1mux_3_o[23:0], {8{pull_resistor_4_node[7]}}}), .P(c32bit2x1mux_3_o), .S(S[3]),
    .O(c32bit2x1mux_4_o));
  Pull_Resistor pull_resistor_5 (.node(pull_resistor_5_node[15]));
  C32Bit2x1Mux c32bit2x1mux_5 (
    .N({c32bit2x1mux_4_o[15:0], {16{pull_resistor_5_node[15]}}}), .P(c32bit2x1mux_4_o), .S(S[4]), .O(O));
endmodule

module C32BitRightShifter (
  input  [4:0] S,
  input  [31:0] P,
  input  AShift,
  output [31:0] O
);

  wire as, pull_resistor_1_node;
  wire [31:0] c32bit2x1mux_1_o, c32bit2x1mux_2_o, c32bit2x1mux_3_o, c32bit2x1mux_4_o;

  Pull_Resistor pull_resistor_1 (.node(pull_resistor_1_node));
  C32Bit2x1Mux c32bit2x1mux_1 (.N({as, P[31:1]}), .P(P), .S(S[0]), .O(c32bit2x1mux_1_o));
  Cmux2x1 cmux2x1_1 (.N(P[31]), .P(pull_resistor_1_node), .S(AShift), .O(as));
  C32Bit2x1Mux c32bit2x1mux_2 (
    .N({{2{as}}, c32bit2x1mux_1_o[31:2]}), .P(c32bit2x1mux_1_o), .S(S[1]), .O(c32bit2x1mux_2_o));
  C32Bit2x1Mux c32bit2x1mux_3 (
    .N({{4{as}}, c32bit2x1mux_2_o[31:4]}), .P(c32bit2x1mux_2_o), .S(S[2]), .O(c32bit2x1mux_3_o));
  C32Bit2x1Mux c32bit2x1mux_4 (
    .N({{8{as}}, c32bit2x1mux_3_o[31:8]}), .P(c32bit2x1mux_3_o), .S(S[3]), .O(c32bit2x1mux_4_o));
  C32Bit2x1Mux c32bit2x1mux_5 (.N({{16{as}}, c32bit2x1mux_4_o[31:16]}), .P(c32bit2x1mux_4_o), .S(S[4]), .O(O));
endmodule

module C32BitALU (
  input  [2:0] opcode,
  input  [31:0] B,
  input  [31:0] A,
  input  ModeAsr,
  output [31:0] O,
  output SF,
  output ZF,
  output CF,
  output OVF
);

  wire and_2_out, and_3_out, pull_resistor_1_node;
  wire [31:0] and_1_out, bit_extender_1_out, c32bit2x1mux_1_o, c32bit2x1mux_2_o, c32bit2x1mux_3_o,
       c32bit2x1mux_4_o, c32bit2x1mux_5_o, c32bit2x1mux_6_o, c32bitadder_1_sum, c32bitadder_2_sum,
       c32bitleftshifter_1_o, c32bitrightshifter_1_o, or_1_out, xor_1_out;

  Pull_Resistor #(.pull(1)) pull_resistor_1 (.node(pull_resistor_1_node));
  assign or_1_out = B | A;  // OR_Gate or_1, 32 bits wide
  assign and_1_out = B & A;  // AND_Gate and_1, 32 bits wide
  assign xor_1_out = B ^ A;  // XOR_Gate xor_1, 32 bits wide
  C32BitAdder c32bitadder_1 (.B(B), .A(A), .Sum(c32bitadder_1_sum), .c(CF));  // open: sub
  C32BitAdder c32bitadder_2 (.B(B), .A(A), .sub(pull_resistor_1_node), .Sum(c32bitadder_2_sum));  // open: c
  C32BitLeftShifter c32bitleftshifter_1 (.S(B[4:0]), .P(A), .O(c32bitleftshifter_1_o));
  C32BitRightShifter c32bitrightshifter_1 (.S(B[4:0]), .P(A), .AShift(ModeAsr), .O(c32bitrightshifter_1_o));
  assign bit_extender_1_out = {{31{c32bitadder_2_sum[31]}}, c32bitadder_2_sum[31]};  // Bit_Extender bit_extender_1
  C32Bit2x1Mux c32bit2x1mux_1 (.N(c32bitadder_1_sum), .P(c32bitadder_2_sum), .S(opcode[0]), .O(c32bit2x1mux_1_o));
  C32Bit2x1Mux c32bit2x1mux_2 (.N(and_1_out), .P(or_1_out), .S(opcode[0]), .O(c32bit2x1mux_2_o));
  C32Bit2x1Mux c32bit2x1mux_3 (.N(xor_1_out), .P(c32bitleftshifter_1_o), .S(opcode[0]), .O(c32bit2x1mux_3_o));
  C32Bit2x1Mux c32bit2x1mux_4 (.N(c32bitrightshifter_1_o), .P(bit_extender_1_out), .S(opcode[0]), .O(c32bit2x1mux_4_o));
  C32Bit2x1Mux c32bit2x1mux_5 (.N(c32bit2x1mux_2_o), .P(c32bit2x1mux_1_o), .S(opcode[1]), .O(c32bit2x1mux_5_o));
  C32Bit2x1Mux c32bit2x1mux_6 (.N(c32bit2x1mux_3_o), .P(c32bit2x1mux_4_o), .S(opcode[1]), .O(c32bit2x1mux_6_o));
  C32Bit2x1Mux c32bit2x1mux_7 (.N(c32bit2x1mux_6_o), .P(c32bit2x1mux_5_o), .S(opcode[2]), .O(O));
  and and_2 (and_2_out, ~A[31], ~B[31], O[31]);  // AND_Gate
  and and_3 (and_3_out, A[31], B[31], ~O[31]);  // AND_Gate
  or or_2 (OVF, and_2_out, and_3_out);
  nor nor_1 (ZF, O[0], O[1], O[2], O[3], O[4], O[5], O[6], O[7], O[8], O[9], O[10], O[11], O[12], O[13], O[14], O[15], O[17], O[18], O[19], O[20], O[21], O[22], O[23], O[24], O[25], O[26], O[27], O[28], O[29], O[30], O[31], O[16]);

  assign SF = O[31];

  // Other names for the same wires on the sheet: sa = A[31]; bhbits[7:0] = B[31:24]; sb = B[31]; so = O[31]
endmodule

module C32Bit8Registers (
  input  C,
  input  [31:0] R1,
  input  W1,
  input  W2,
  input  W3,
  input  W4,
  input  W5,
  input  W6,
  input  W7,
  input  [31:0] R2,
  input  [31:0] R3,
  input  [31:0] R4,
  input  [31:0] R5,
  input  [31:0] R6,
  input  [31:0] R7,
  output [31:0] Q1,
  output [31:0] Q2,
  output [31:0] Q3,
  output [31:0] Q4,
  output [31:0] Q5,
  output [31:0] Q6,
  output [31:0] Q7
);

  D32bitRegister d32bitregister_1 (.E(W1), .C(C), .Num(R1), .Q(Q1));  // open: QN
  D32bitRegister d32bitregister_2 (.E(W2), .C(C), .Num(R2), .Q(Q2));  // open: QN
  D32bitRegister d32bitregister_3 (.E(W3), .C(C), .Num(R3), .Q(Q3));  // open: QN
  D32bitRegister d32bitregister_4 (.E(W4), .C(C), .Num(R4), .Q(Q4));  // open: QN
  D32bitRegister d32bitregister_5 (.E(W5), .C(C), .Num(R5), .Q(Q5));  // open: QN
  D32bitRegister d32bitregister_6 (.E(W6), .C(C), .Num(R6), .Q(Q6));  // open: QN
  D32bitRegister d32bitregister_7 (.E(W7), .C(C), .Num(R7), .Q(Q7));  // open: QN
endmodule

module Cmux8x1 (
  input  I0,
  input  I1,
  input  I2,
  input  I3,
  input  I4,
  input  I5,
  input  I6,
  input  I7,
  input  s2,
  input  s1,
  input  s0,
  output o
);

  wire and_1_out, and_2_out, and_3_out, and_4_out, and_5_out, and_6_out, and_7_out, and_8_out, not_1_out,
       not_2_out, not_3_out;

  not not_1 (not_1_out, s2);
  not not_2 (not_2_out, s1);
  not not_3 (not_3_out, s0);
  and and_1 (and_1_out, I0, not_3_out, not_2_out, not_1_out);
  and and_2 (and_2_out, I1, not_2_out, not_1_out, s0);
  and and_3 (and_3_out, I5, s2, not_2_out, s0);
  and and_4 (and_4_out, I6, s2, s1, not_3_out);
  and and_5 (and_5_out, I7, s2, s1, s0);
  and and_6 (and_6_out, I2, not_1_out, s1, not_3_out);
  and and_7 (and_7_out, I3, not_1_out, s0, s1);
  and and_8 (and_8_out, I4, s2, not_3_out, not_2_out);
  or or_1 (o, and_1_out, and_2_out, and_6_out, and_7_out, and_8_out, and_3_out, and_4_out, and_5_out);
endmodule

module C32BitRegisterFile (
  input  C,
  input  [31:0] R,
  input  [2:0] SA,
  input  EW,
  input  [2:0] SR,
  input  [2:0] SB,
  output [31:0] A,
  output [31:0] B
);

  wire and_1_out, and_2_out, and_3_out, and_4_out, and_5_out, and_6_out, and_7_out, c8x3decoder_1_d0, D1, D2,
       D3, D4, D5, D6, D7;
  wire [31:0] c32bit2x1mux_1_o, c32bit2x1mux_2_o, c32bit2x1mux_3_o, c32bit2x1mux_4_o, c32bit2x1mux_5_o,
       c32bit2x1mux_6_o, c32bit2x1mux_7_o, c32bit2x1mux_8_o, c32bit2x1mux_9_o, c32bit2x1mux_10_o,
       c32bit2x1mux_11_o, c32bit2x1mux_12_o, R1, R2, R3, R4, R5, R6, R7;

  and and_1 (and_1_out, D1, EW);
  and and_2 (and_2_out, D2, EW);
  and and_3 (and_3_out, D3, EW);
  C8x3Decoder c8x3decoder_1 (
    .s2(SR[2]), .s1(SR[1]), .s0(SR[0]), .D0(c8x3decoder_1_d0), .D1(D1), .D2(D2), .D3(D3), .D4(D4), .D5(D5),
    .D6(D6), .D7(D7));
  C32Bit8Registers c32bit8registers_1 (
    .C(C), .R1(R), .W1(and_1_out), .W2(and_2_out), .W3(and_3_out), .W4(and_4_out), .W5(and_5_out),
    .W6(and_6_out), .W7(and_7_out), .R2(R), .R3(R), .R4(R), .R5(R), .R6(R), .R7(R), .Q1(R1), .Q2(R2),
    .Q3(R3), .Q4(R4), .Q5(R5), .Q6(R6), .Q7(R7));
  and and_4 (and_4_out, D4, EW);
  and and_5 (and_5_out, D5, EW);
  and and_6 (and_6_out, D6, EW);
  and and_7 (and_7_out, D7, EW);
  C32Bit2x1Mux c32bit2x1mux_1 (.N(R1), .P({32{1'b0}}), .S(SB[0]), .O(c32bit2x1mux_1_o));
  C32Bit2x1Mux c32bit2x1mux_2 (.N(R3), .P(R2), .S(SB[0]), .O(c32bit2x1mux_2_o));
  C32Bit2x1Mux c32bit2x1mux_3 (.N(R5), .P(R4), .S(SB[0]), .O(c32bit2x1mux_3_o));
  C32Bit2x1Mux c32bit2x1mux_4 (.N(R7), .P(R6), .S(SB[0]), .O(c32bit2x1mux_4_o));
  C32Bit2x1Mux c32bit2x1mux_5 (.N(R1), .P({32{1'b0}}), .S(SA[0]), .O(c32bit2x1mux_5_o));
  C32Bit2x1Mux c32bit2x1mux_6 (.N(R3), .P(R2), .S(SA[0]), .O(c32bit2x1mux_6_o));
  C32Bit2x1Mux c32bit2x1mux_7 (.N(R5), .P(R4), .S(SA[0]), .O(c32bit2x1mux_7_o));
  C32Bit2x1Mux c32bit2x1mux_8 (.N(R7), .P(R6), .S(SA[0]), .O(c32bit2x1mux_8_o));
  C32Bit2x1Mux c32bit2x1mux_9 (.N(c32bit2x1mux_2_o), .P(c32bit2x1mux_1_o), .S(SB[1]), .O(c32bit2x1mux_9_o));
  C32Bit2x1Mux c32bit2x1mux_10 (.N(c32bit2x1mux_4_o), .P(c32bit2x1mux_3_o), .S(SB[1]), .O(c32bit2x1mux_10_o));
  C32Bit2x1Mux c32bit2x1mux_11 (.N(c32bit2x1mux_6_o), .P(c32bit2x1mux_5_o), .S(SA[1]), .O(c32bit2x1mux_11_o));
  C32Bit2x1Mux c32bit2x1mux_12 (.N(c32bit2x1mux_8_o), .P(c32bit2x1mux_7_o), .S(SA[1]), .O(c32bit2x1mux_12_o));
  C32Bit2x1Mux c32bit2x1mux_13 (.N(c32bit2x1mux_10_o), .P(c32bit2x1mux_9_o), .S(SB[2]), .O(B));
  C32Bit2x1Mux c32bit2x1mux_14 (.N(c32bit2x1mux_12_o), .P(c32bit2x1mux_11_o), .S(SA[2]), .O(A));
endmodule

module C8x3Decoder (
  input  s2,
  input  s1,
  input  s0,
  output D0,
  output D1,
  output D2,
  output D3,
  output D4,
  output D5,
  output D6,
  output D7
);

  wire not_1_out, not_2_out, not_3_out;

  not not_1 (not_1_out, s2);
  not not_2 (not_2_out, s1);
  not not_3 (not_3_out, s0);
  and and_1 (D0, not_3_out, not_2_out, not_1_out);
  and and_2 (D1, not_2_out, not_1_out, s0);
  and and_3 (D2, not_1_out, s1, not_3_out);
  and and_4 (D3, not_1_out, s0, s1);
  and and_5 (D4, s2, not_3_out, not_2_out);
  and and_6 (D5, s2, not_2_out, s0);
  and and_7 (D6, s2, s1, not_3_out);
  and and_8 (D7, s2, s1, s0);
endmodule

module C32bitPcCounter (
  input  [31:0] pcup,
  input  sub,
  input  C,
  output [31:0] PC
);

  wire or_1_out, por_1_out;
  wire [31:0] c32bit2x1mux_1_o, c32bitadder_1_sum;

  Pull_Resistor pull_resistor_1 (.node(C));
  or or_1 (or_1_out, por_1_out, C);
  POR #(.PorHighDuration(1)) por_1 (.out(por_1_out));
  C32Bit2x1Mux c32bit2x1mux_1 (.N({32{1'b0}}), .P(c32bitadder_1_sum), .S(por_1_out), .O(c32bit2x1mux_1_o));
  C32BitAdder c32bitadder_1 (.B(pcup), .A(PC), .sub(sub), .Sum(c32bitadder_1_sum));  // open: c
  D32bitRegister d32bitregister_1 (.E(1'b1), .C(or_1_out), .Num(c32bit2x1mux_1_o), .Q(PC));  // open: QN
endmodule

module CROM3X8 (
  input  in_1,
  input  in_2,
  input  in_3
);

  wire d0, d1, d2, d3, d4, d5, d6, d7, pull_resistor_1_node, pull_resistor_2_node, pull_resistor_3_node,
       pull_resistor_4_node, pull_resistor_5_node, pull_resistor_6_node, pull_resistor_7_node,
       pull_resistor_8_node;

  // OR_Gate or_1 has open pins: in1=pull_resistor_4_node, out=open
  // OR_Gate or_2 has open pins: in0=d0, in1=pull_resistor_4_node, out=open
  // OR_Gate or_3 has open pins: in0=d1, in1=pull_resistor_5_node, out=open
  // OR_Gate or_4 has open pins: in1=pull_resistor_6_node, out=open
  // OR_Gate or_5 has open pins: in1=pull_resistor_7_node, out=open
  // OR_Gate or_6 has open pins: in1=pull_resistor_7_node, out=open
  // OR_Gate or_7 has open pins: in1=pull_resistor_1_node, out=open
  // OR_Gate or_8 has open pins: in1=pull_resistor_1_node, out=open
  // OR_Gate or_9 has open pins: in1=pull_resistor_2_node, out=open
  // OR_Gate or_10 has open pins: in1=pull_resistor_2_node, out=open
  // OR_Gate or_11 has open pins: in1=pull_resistor_3_node, out=open
  // OR_Gate or_12 has open pins: in1=pull_resistor_3_node, out=open
  // OR_Gate or_13 has open pins: in1=pull_resistor_8_node, out=open
  // OR_Gate or_14 has open pins: in1=pull_resistor_4_node, out=open
  // OR_Gate or_15 has open pins: in1=pull_resistor_4_node, out=open
  // OR_Gate or_16 has open pins: in1=pull_resistor_5_node, out=open
  // OR_Gate or_17 has open pins: in1=pull_resistor_5_node, out=open
  // OR_Gate or_18 has open pins: in1=pull_resistor_6_node, out=open
  // OR_Gate or_19 has open pins: in1=pull_resistor_6_node, out=open
  // OR_Gate or_20 has open pins: in1=pull_resistor_7_node, out=open
  // OR_Gate or_21 has open pins: in1=pull_resistor_1_node, out=open
  // OR_Gate or_22 has open pins: in1=pull_resistor_2_node, out=open
  // OR_Gate or_23 has open pins: in1=pull_resistor_3_node, out=open
  // OR_Gate or_24 has open pins: in1=pull_resistor_8_node, out=open
  // OR_Gate or_25 has open pins: in1=pull_resistor_8_node, out=open
  // OR_Gate or_26 has open pins: in1=pull_resistor_4_node, out=open
  // OR_Gate or_27 has open pins: in1=pull_resistor_4_node, out=open
  // OR_Gate or_28 has open pins: in1=pull_resistor_5_node, out=open
  // OR_Gate or_29 has open pins: in1=pull_resistor_5_node, out=open
  // OR_Gate or_30 has open pins: in1=pull_resistor_6_node, out=open
  // OR_Gate or_31 has open pins: in1=pull_resistor_6_node, out=open
  // OR_Gate or_32 has open pins: in1=pull_resistor_7_node, out=open
  // OR_Gate or_33 has open pins: in1=pull_resistor_7_node, out=open
  // OR_Gate or_34 has open pins: in1=pull_resistor_1_node, out=open
  // OR_Gate or_35 has open pins: in1=pull_resistor_1_node, out=open
  // OR_Gate or_36 has open pins: in1=pull_resistor_2_node, out=open
  // OR_Gate or_37 has open pins: in1=pull_resistor_2_node, out=open
  // OR_Gate or_38 has open pins: in1=pull_resistor_3_node, out=open
  // OR_Gate or_39 has open pins: in1=pull_resistor_3_node, out=open
  // OR_Gate or_40 has open pins: in1=pull_resistor_8_node, out=open
  // OR_Gate or_41 has open pins: in1=pull_resistor_8_node, out=open
  C8x3Decoder c8x3decoder_1 (
    .s2(in_1), .s1(in_2), .s0(in_3), .D0(d0), .D1(d1), .D2(d2), .D3(d3), .D4(d4), .D5(d5), .D6(d6), .D7(d7));
  // OR_Gate or_42 has open pins: in1=pull_resistor_4_node, out=open
  // OR_Gate or_43 has open pins: in1=pull_resistor_4_node, out=open
  // OR_Gate or_44 has open pins: in1=pull_resistor_5_node, out=open
  // OR_Gate or_45 has open pins: in1=pull_resistor_5_node, out=open
  // OR_Gate or_46 has open pins: in1=pull_resistor_6_node, out=open
  // OR_Gate or_47 has open pins: in1=pull_resistor_6_node, out=open
  // OR_Gate or_48 has open pins: in1=pull_resistor_7_node, out=open
  // OR_Gate or_49 has open pins: in1=pull_resistor_7_node, out=open
  // OR_Gate or_50 has open pins: in1=pull_resistor_1_node, out=open
  // OR_Gate or_51 has open pins: in1=pull_resistor_1_node, out=open
  // OR_Gate or_52 has open pins: in1=pull_resistor_2_node, out=open
  // OR_Gate or_53 has open pins: in1=pull_resistor_2_node, out=open
  // OR_Gate or_54 has open pins: in1=pull_resistor_3_node, out=open
  // OR_Gate or_55 has open pins: in1=pull_resistor_3_node, out=open
  // OR_Gate or_56 has open pins: in1=pull_resistor_8_node, out=open
  // OR_Gate or_57 has open pins: in1=pull_resistor_8_node, out=open
  Pull_Resistor pull_resistor_1 (.node(pull_resistor_1_node));
  Pull_Resistor pull_resistor_2 (.node(pull_resistor_2_node));
  Pull_Resistor pull_resistor_3 (.node(pull_resistor_3_node));
  Pull_Resistor pull_resistor_4 (.node(pull_resistor_4_node));
  Pull_Resistor pull_resistor_5 (.node(pull_resistor_5_node));
  Pull_Resistor pull_resistor_6 (.node(pull_resistor_6_node));
  Pull_Resistor pull_resistor_7 (.node(pull_resistor_7_node));
  Pull_Resistor pull_resistor_8 (.node(pull_resistor_8_node));
endmodule

module CCu (
  input  in_1,
  input  in_2,
  input  [1:0] in_3,
  input  [2:0] in_4,
  output [31:0] out_5,
  output [31:0] out_6,
  output [31:0] out_7
);

  wire addpc, and_1_out, and_2_out, and_3_out, calu, calu2, cbra, cimme, cmemr, cmemw, cregdest, cregw, i0,
       i1, i2, i3, i4, i5, i6, i7, i8, i9, i10, i11, i12, i13, i14, i15, i16, i17, i18, i19, i20, i21, i22,
       i23, i24, i25, i26, i27, i28, i29, i30, i31, or_1_out, sf, sf2, zf, zf2;
  wire [2:0] multiplexer_1_out, SA, SR;
  wire [31:0] B, bit_extender_1_out, bit_extender_2_out, Br, c32bitalu_1_o, pc, pcup, ramo, vaddpc;

  C32bitPcCounter c32bitpccounter_1 (.pcup(pcup), .sub(in_2), .C(in_1), .PC(pc));
  C32BitRegisterFile c32bitregisterfile_1 (
    .C(in_1), .R(out_5), .SA(SA), .EW(cregw), .SR(SR), .SB({i19, i18, i17}), .A(out_6), .B(Br));
  ROM #(.addrWidth(16), .dataWidth(32)) rom_1 (
    .addr(pc[15:0]),
    .data({i31, i30, i29, i28, i27, i26, i25, i24, i23, i22, i21, i20, i19, i18, i17, i16, i15, i14, i13, i12, i11, i10, i9, i8, i7, i6, i5, i4, i3, i2, i1, i0}));
  assign bit_extender_1_out = {{24{1'b0}}, {i7, i6, i5, i4, i3, i2, i1, i0}};  // Bit_Extender bit_extender_1
  RAM #(.dataWidth(32)) ram_1 (
    .addr({i7, i6, i5, i4, i3, i2, i1, i0}), .we(cmemw), .oe(cmemr), .clk(in_1), .din(out_6), .dout(ramo));
  C32Bit2x1Mux c32bit2x1mux_1 (.N(vaddpc), .P(32'h1), .S(addpc), .O(pcup));
  C32BitAdder c32bitadder_1 (.B(pc), .A(bit_extender_1_out), .sub(1'b1), .Sum(vaddpc));  // open: c
  and and_1 (and_1_out, i29, ~i30, i31, zf2);  // AND_Gate
  and and_2 (and_2_out, i29, ~i30, ~i31, sf2);  // AND_Gate
  and and_3 (and_3_out, ~i29, i30, i31);  // AND_Gate
  ROM #(.addrWidth(3)) rom_2 (.addr({i31, i30, i29}), .data({calu, calu2, cregw, cimme, cbra, cmemr, cmemw, cregdest}));
  or or_1 (or_1_out, and_1_out, and_2_out, and_3_out);
  Multiplexer #(.width(3)) multiplexer_1 (.in0({i28, i27, i26}), .in1(3'b001), .out(multiplexer_1_out), .sel(cimme));
  and and_4 (addpc, cbra, or_1_out);
  C32BitALU c32bitalu_1 (
    .opcode(multiplexer_1_out), .B(B), .A(out_6), .O(c32bitalu_1_o), .SF(sf), .ZF(zf));  // open: ModeAsr, CF, OVF
  Multiplexer #(.width(32)) multiplexer_2 (.in0(c32bitalu_1_o), .in1(ramo), .out(out_5), .sel(cmemr));
  assign bit_extender_2_out = {{6{1'b0}}, {i25, i24, i23, i22, i21, i20, i19, i18, i17, i16, i15, i14, i13, i12, i11, i10, i9, i8, i7, i6, i5, i4, i3, i2, i1, i0}};  // Bit_Extender bit_extender_2
  Multiplexer #(.width(3)) multiplexer_3 (.in0({i25, i24, i23}), .in1({i28, i27, i26}), .out(SR), .sel(cregdest));
  Multiplexer #(.width(32)) multiplexer_4 (.in0(Br), .in1(bit_extender_2_out), .out(B), .sel(cimme));
  Multiplexer #(.select(2), .width(3)) multiplexer_5 (
    .in0(3'b000), .in1({i28, i27, i26}), .in2({i22, i21, i20}), .in3(in_4), .out(SA), .sel({calu, calu2}));
  CDflipFlop cdflipflop_1 (.C(in_1), .D(sf), .E(1'b1), .Q(sf2));  // open: QN
  CDflipFlop cdflipflop_2 (.C(in_1), .D(zf), .E(1'b1), .Q(zf2));  // open: QN

  assign out_7 = out_6;

  // Other names for the same wires on the sheet: SB[2:0] = {i19, i18, i17}; Ar[31:0] = out_6; clo = in_1;
  //   R[31:0] = out_5

  // Notes on the sheet:
  //   contents of rom_1 (hex, n*v repeats v):
  //   e8000000 ec000005 f0000006 f4000002 f8000006 fc000006 6b80000 27c0000 20000001
  //   contents of rom_2 (hex, n*v repeats v):
  //   a0 d8 31 35 52 d8 d8 31
endmodule
