// Logisim project FullAdderCustom.circ as structural Verilog: 5 circuits, main circuit CFullAdder
module CFullAdder (
  input  a,
  input  b,
  input  cin,
  output sum,
  output cout
);

  wire and_1_out, and_2_out, xor_1_out;

  xor xor_1 (xor_1_out, a, b);
  xor xor_2 (sum, xor_1_out, cin);
  and and_1 (and_1_out, xor_1_out, cin);
  and and_2 (and_2_out, a, b);
  or or_1 (cout, and_1_out, and_2_out);
endmodule

module C4BitAdder (
  input  [3:0] B,
  input  cin,
  input  [3:0] A,
  output [3:0] sum,
  output cout
);

  wire cfulladder_2_cout, cfulladder_3_cout, cfulladder_4_cout;

  CFullAdder cfulladder_1 (.a(A[3]), .b(B[3]), .cin(cfulladder_2_cout), .sum(sum[3]), .cout(cout));
  CFullAdder cfulladder_2 (.a(A[2]), .b(B[2]), .cin(cfulladder_3_cout), .sum(sum[2]), .cout(cfulladder_2_cout));
  CFullAdder cfulladder_3 (.a(A[1]), .b(B[1]), .cin(cfulladder_4_cout), .sum(sum[1]), .cout(cfulladder_3_cout));
  CFullAdder cfulladder_4 (.a(A[0]), .b(B[0]), .cin(cin), .sum(sum[0]), .cout(cfulladder_4_cout));
endmodule

module C8bitAdder (
  input  cin,
  input  [7:0] A,
  input  [7:0] B,
  output [7:0] Sum,
  output cout
);

  wire c4bitadder_2_cout;

  C4BitAdder c4bitadder_1 (.B(B[7:4]), .cin(c4bitadder_2_cout), .A(A[7:4]), .sum(Sum[7:4]), .cout(cout));
  C4BitAdder c4bitadder_2 (.B(B[3:0]), .cin(cin), .A(A[3:0]), .sum(Sum[3:0]), .cout(c4bitadder_2_cout));
endmodule

module C16BitAdder (
  input  [15:0] B,
  input  [15:0] A,
  input  cin,
  output [15:0] Sum,
  output cout
);

  wire c8bitadder_2_cout;

  C8bitAdder c8bitadder_1 (.cin(c8bitadder_2_cout), .A(A[15:8]), .B(B[15:8]), .Sum(Sum[15:8]), .cout(cout));
  C8bitAdder c8bitadder_2 (.cin(cin), .A(A[7:0]), .B(B[7:0]), .Sum(Sum[7:0]), .cout(c8bitadder_2_cout));
endmodule

module C32BitAdder (
  input  [31:0] B,
  input  [31:0] A,
  input  sub,
  output [31:0] Sum,
  output c
);

  wire c16bitadder_2_cout;
  wire [15:0] xor_1_out, xor_1_out_2;
  wire [31:0] bit_extender_1_out;

  assign {xor_1_out_2, xor_1_out} = B ^ bit_extender_1_out;  // XOR_Gate xor_1, 32 bits wide
  assign bit_extender_1_out = {{31{sub}}, sub};  // Bit_Extender bit_extender_1
  C16BitAdder c16bitadder_1 (.B(xor_1_out_2), .A(A[31:16]), .cin(c16bitadder_2_cout), .Sum(Sum[31:16]), .cout(c));
  C16BitAdder c16bitadder_2 (.B(xor_1_out), .A(A[15:0]), .cin(sub), .Sum(Sum[15:0]), .cout(c16bitadder_2_cout));
endmodule
