// Logisim project andWIthTransistors.circ as structural Verilog: 1 circuit, main circuit main
module main (
  input  in_1,
  input  in_2,
  input  in_3
);

  wire not_1_out, not_2_out, switch_1_p2, switch_2_p3, switch_2_p4, transistor_1_out, transistor_2_out,
       transistor_3_out, transistor_4_out;

  // Switch switch_1: pin names not known; wires that end beside it: 1'b1, switch_1_p2
  Transistor transistor_1 (.in(1'b1), .out(transistor_1_out), .gate(switch_1_p2));
  not not_1 (not_1_out, in_2);
  Transistor transistor_2 (.in(in_3), .out(transistor_2_out), .gate(not_1_out));
  Pull_Resistor pull_resistor_1 (.node(switch_1_p2));
  // Switch switch_2: pin names not known; wires that end beside it: in_3, 1'b1, switch_2_p3, switch_2_p4, switch_2_p4
  Transistor transistor_3 (.in(transistor_1_out), .out(transistor_3_out), .gate(switch_2_p3));
  Transistor transistor_4 (.in(transistor_2_out), .out(transistor_4_out), .gate(not_2_out));
  Pull_Resistor pull_resistor_2 (.node(switch_2_p3));
  not not_2 (not_2_out, in_1);
  LED led_1 (.in(transistor_4_out));
  LED led_2 (.in(transistor_3_out));
endmodule
